# Fritzing sketch photoresistance (saved by Fritzing 0.9.3b)

parts:
  part = Resistor [tolerance=±5% resistance=100k package=THT]
  Photorésistance = Photocell (LDR) [package=THT]

nets:
  5V: part.Pin_0
  out: part.Pin_1, Photorésistance.pin_1
  GND: Photorésistance.pin_0
