# Fritzing sketch bande_del (saved by Fritzing 0.9.3b)

parts:
  NEOPIXEL1 = Neopixel Strip -- Black (30/m) [part_number=1376]  # not connected
  NEOPIXEL3 = Neopixel Strip -- Black (60/m) [part_number=1461]  # not connected
  DOTSTAR1 = DotStar Strip -- Black (60/m) [part_number=2239]  # not connected
  NEOPIXEL4 = Neopixel Strip -- Black (60/m) [part_number=1461]
  NEOPIXEL5 = Neopixel Strip -- Black (30/m) [part_number=1376]
  DOTSTAR2 = DotStar Strip -- Black (60/m) [part_number=2239]
  NEOPIXEL6 = Neopixel Strip -- Black (30/m) [part_number=1376]
  DOTSTAR3 = DotStar Strip -- Black (60/m) [part_number=2239]
  NEOPIXEL7 = Neopixel Strip -- Black (60/m) [part_number=1461]

nets:
  N1: NEOPIXEL4.+5V, NEOPIXEL7.+5V#6
  N2: NEOPIXEL4.DI, NEOPIXEL7.DO
  N3: NEOPIXEL4.GND, NEOPIXEL7.GND#4
  N4: NEOPIXEL5.GND, NEOPIXEL6.GND#6
  N5: NEOPIXEL5.Din, NEOPIXEL6.Dout
  N6: NEOPIXEL5.+5V, NEOPIXEL6.+5V#4
  N7: DOTSTAR2.+5V, DOTSTAR3.+5V#6
  N8: DOTSTAR2.DI, DOTSTAR3.DO
  N9: DOTSTAR2.GND, DOTSTAR3.GND#4
  N10: DOTSTAR2.CI, DOTSTAR3.CO

custom parts:
  Neopixel Strip -- Black (30/m): These NeoPixel strips have 30 digitally-addressable pixel LEDs per meter and are very affordable and are only 12.5 mm wide, 10 mm if you remove the strip from the casing.
  Neopixel Strip -- Black (60/m): Neopixel Strip, Black, 60 pixels per meter.
  DotStar Strip -- Black (60/m): NeopixelDotStar Strip, Black, 60 pixels per meter.
