# Fritzing sketch circuit (saved by Fritzing 0.9.3b)
breadboards: 1

parts:
  S1 = Pushbutton [package="[THT]"]
  LED1 = LED - 5mm [color="Red (633nm)" package="5 mm [THT]"]
  Arduino = Arduino Nano (Rev3.0) (ICSP)

nets:
  N1: S1.Pin_1, S1.Pin_2, Arduino.D2
  GND: S1.Pin_3, S1.Pin_4, LED1.cathode, Arduino.GND
  N2: LED1.anode, Arduino.D3
  5V: Arduino.5V
