# Fritzing sketch pong_1d (saved by Fritzing 0.9.3b)
breadboards: 1

parts:
  DOTSTAR1 = DotStar Strip -- Black (60/m) [part_number=2239]
  Composant1 = Arduino Nano (Rev3.0)  # not connected
  JACK1 = 2.1mm Barrel Jack with Terminal Block
  BUTTON1 = Arcade Button (red)  # not connected
  BUTTON2 = Arcade Button (white)  # not connected

nets:
  N1: DOTSTAR1.+5V, JACK1.POS
  N2: DOTSTAR1.GND, JACK1.NEG

custom parts:
  DotStar Strip -- Black (60/m): NeopixelDotStar Strip, Black, 60 pixels per meter.
  Arcade Button (red): Adafruit Arcade Button (red)
  Arcade Button (white): Adafruit Arcade Button (white)
